// Logisim project control_logic.circ as structural Verilog: 2 circuits, main circuit control_logic
module control_logic (
  input  [31:0] inst,
  input  BrEq,
  input  BrLt,
  output PCSel,
  output RegWEn,
  output [2:0] ImmSel,
  output BrUn,
  output ASel,
  output BSel,
  output [3:0] ALUSel,
  output MemRW,
  output [1:0] WBSel,
  output CSRSel,
  output CSRWen
);

  not not_1 (BSel, inst[5]);
  ALU_Decode alu_decode_1 (.funct3(inst[14:12]), .mul_Sel(inst[25]), .SignBit(inst[30]), .ALUSel(ALUSel));

  assign RegWEn = 1'b1;

  // Other names for the same wires on the sheet: Opcode[6:0] = inst[6:0]; rd[4:0] = inst[11:7];
  //   Funct3[2:0] = inst[14:12]; rs1[4:0] = inst[19:15]; rs2[4:0] = inst[24:20]; Funct7[6:0] = inst[31:25]

  // Notes on the sheet:
  //   INPUTS to your circuit
  //   DON'T CHANGE THE LOCATIONS OF THE INPUTS AND OUTPUTS!
  //   OUTPUT from your circuit
endmodule

module ALU_Decode (
  input  [2:0] funct3,
  input  mul_Sel,
  input  SignBit,
  output [3:0] ALUSel
);

  wire [3:0] addOrSubOrMul, sllOrMulh, sltuOrMulhu, sra_l_0;

  Multiplexer #(.enable("false"), .width(4)) multiplexer_1 (.in0(4'b0100), .in1(4'b0101), .out(sra_l_0), .sel(SignBit));
  Multiplexer #(.enable("false"), .select(3), .width(4)) multiplexer_2 (
    .in0(addOrSubOrMul), .in1(sllOrMulh), .in2(4'b0111), .in3(sltuOrMulhu), .in4(4'b0011), .in5(sra_l_0),
    .in6(4'b0010), .in7(4'b0001), .out(ALUSel), .sel(funct3));
  Multiplexer #(.enable("false"), .select(2), .width(4)) multiplexer_3 (
    .in0(4'b0000), .in1(4'b1010), .in2(4'b1100), .out(addOrSubOrMul), .sel({SignBit, mul_Sel}));  // open: in3
  Multiplexer #(.enable("false"), .width(4)) multiplexer_4 (
    .in0(4'b0110), .in1(4'b1110), .out(sllOrMulh), .sel(mul_Sel));
  Multiplexer #(.enable("false"), .width(4)) multiplexer_5 (
    .in0(4'b0111), .in1(4'b1011), .out(sltuOrMulhu), .sel(mul_Sel));

  // Other names for the same wires on the sheet: MS = mul_Sel; S = SignBit
endmodule
