// Logisim project cpu.circ as structural Verilog: 1 circuit, main circuit cpu
module cpu (
  input  clk,
  input  [31:0] INSTRUCTION,
  input  [31:0] READ_DATA,
  output [31:0] WRITE_ADDRESS,
  output [31:0] PROGRAM_COUNTER,
  output [31:0] ra,
  output [31:0] sp,
  output [31:0] t0,
  output [31:0] t1,
  output [31:0] t2,
  output [31:0] s0,
  output [31:0] s1,
  output [31:0] a0,
  output [31:0] tohost,
  output [3:0] WRITE_ENABLE,
  output [31:0] WRITE_DATA
);

  wire BSel, RegWEn;
  wire [3:0] ALUSel;
  wire [31:0] adder_1_out, Immediate, multiplexer_1_out, Reg_Ins, rs1_Value, rs2_Value, WriteToReg;

  Adder #(.width(32)) adder_1 (.a(PROGRAM_COUNTER), .b(32'h4), .out(adder_1_out));  // open: cin, cout
  Register #(.width(32)) PC (.D(adder_1_out), .clk(clk), .Q(PROGRAM_COUNTER));  // open: en, clr
  Register #(.width(32)) register_1 (.D(INSTRUCTION), .clk(clk), .Q(Reg_Ins));  // open: en, clr
  control_logic control_logic_1 (
    .RegWEn(RegWEn), .BSel(BSel), .ALUSel(ALUSel), .inst(Reg_Ins));  // open: CSRWen, PCSel, ImmSel, BrUn, ASel, MemRW, WBSel, CSRSel, BrEq, BrLt
  imm_gen imm_gen_1 (.inst(Reg_Ins), .imm(Immediate));  // open: ImmSel
  regfile regfile_1 (
    .rs1(Reg_Ins[19:15]), .rs2(Reg_Ins[24:20]), .rd(Reg_Ins[11:7]), .Write_Data(WriteToReg), .RegWEn(RegWEn),
    .clk(clk), .ra(ra), .sp(sp), .t0(t0), .t1(t1), .t2(t2), .s0(s0), .s1(s1), .a0(a0),
    .Read_Data_1(rs1_Value), .Read_Data_2(rs2_Value));
  // branch_comp branch_comp_1: pin names not known
  Multiplexer #(.enable("false"), .width(32)) multiplexer_1 (
    .in0(rs2_Value), .in1(Immediate), .out(multiplexer_1_out), .sel(BSel));
  alu alu_1 (.Result(WriteToReg), .A(rs1_Value), .B(multiplexer_1_out), .ALUSel(ALUSel));
  csr csr_1 (.tohost(tohost));  // open: CSR_address, CSR_din, CSR_WE, clk

  // Notes on the sheet:
  //   Output to IMEM
  //   IMEM (do **NOT** move this)
  //   Inputs from IMEM
  //   It is OK to move the PC, RegFile, ALU, MEM, Branch Comp, Imm Gen, and Control Logic to wherever is most convenient for you when constructing your CPU, and to delete this text
  //   Inputs/Outputs for testing. Do **NOT** move these.
  //   Outputs To DMEM
  //   DMEM (do **NOT** move this)
  //   Inputs From DMEM
endmodule
