// Logisim project imm_gen.circ as structural Verilog: 1 circuit, main circuit imm_gen
module imm_gen (
  input  [31:0] inst,
  input  [2:0] ImmSel,
  output [31:0] imm
);

  wire [31:0] I_Imm, S_Imm;

  assign I_Imm = {{20{inst[31]}}, inst[31:20]};  // Bit_Extender bit_extender_1
  assign S_Imm = {{20{inst[31]}}, {inst[31:25], inst[11:7]}};  // Bit_Extender bit_extender_2
  Multiplexer #(.enable("false"), .select(3), .width(32)) multiplexer_1 (
    .in0({32{1'b0}}), .in1(I_Imm), .in2(S_Imm), .out(imm), .sel(ImmSel));  // open: in3, in4, in5, in6, in7

  // Other names for the same wires on the sheet: Immediate[31:0] = imm

  // Notes on the sheet:
  //   INPUTS to your circuit
  //   DON'T CHANGE THE LOCATIONS OF THE INPUTS AND OUTPUTS!
  //   OUTPUT from your circuit
endmodule
