// Logisim project Test.circ as structural Verilog: 2 circuits, main circuit main
module main (
);

  Extend extend_1 ();  // open: in_1, EightBits, out_3, Output24_31
endmodule

module Extend (
  input  [31:0] in_1,
  output [7:0] EightBits,
  output [63:0] out_3,
  output [7:0] Output24_31
);

  Adder adder_1 (.a(in_1[7:0]), .b(in_1[15:8]), .out(EightBits));  // open: cin, cout
  assign out_3 = {{32{in_1[31]}}, in_1};  // Bit_Extender bit_extender_1

  assign Output24_31 = in_1[31:24];

  // Other names for the same wires on the sheet: Bits16_23[7:0] = in_1[23:16]; Bits24_31[7:0] = in_1[31:24]
endmodule
